# Fritzing sketch Authentication System V1 (saved by Fritzing 0.9.3b)

parts:
  Part1 = Arduino Uno (Rev3)
  Part2 = 4x4 Keypad [part_number=101207]
  Part3 = LCD1602-I2C

nets:
  N1: Part1.D8, Part2.8
  N2: Part1.D9_PWM, Part2.7
  N3: Part1.D10_PWM/SS, Part2.6
  N4: Part1.D11_PWM/MOSI, Part2.5
  GND: Part1.GND, Part3.GND
  N5: Part1.A4/SDA, Part3.SDA
  N6: Part1.A5/SCL, Part3.SCL
  N7: Part1.D2, Part2.4
  N8: Part1.D3_PWM, Part2.3
  N9: Part1.D4, Part2.2
  N10: Part1.D5_PWM, Part2.1
  5V: Part1.5V, Part3.VCC

custom parts:
  4x4 Keypad: Matrix membrane keypad 4x4
  LCD1602-I2C: A standard character display, usually with 2x16 characters. Comes in many colors with LCM1602 IIC attached.
